// Logisim project cpu.circ as structural Verilog: 2 circuits, main circuit datapath
module datapath (
  input  pcsrc,
  input  mdrload,
  input  mem2reg,
  input  pcload,
  input  regwrite,
  input  [2:0] opc,
  input  sub,
  input  IOrD,
  input  ALoad,
  input  alusrc1,
  input  regsrc2,
  input  aluoutload,
  input  IRload,
  input  [4:0] rs1,
  input  [4:0] rs2,
  input  [4:0] rd,
  input  BLoad,
  input  [1:0] alusrc2,
  input  MemWr,
  input  MemRd,
  input  [31:0] imm,
  input  [1:0] width,
  input  Extend,
  input  in_24,
  output z,
  output c,
  output [31:0] Inst
);

  wire cd;
  wire [4:0] multiplexer_4_out;
  wire [31:0] alu_1_res, b, memory_1_data, multiplexer_1_out, multiplexer_2_out, multiplexer_3_out,
       multiplexer_5_out, multiplexer_6_out, regfile_1_r1_d, regfile_1_r2_d, register_1_q, register_2_q,
       register_4_q, register_6_q;

  Multiplexer #(.width(32), .enable("false")) multiplexer_1 (
    .in0(register_6_q), .in1(alu_1_res), .out(multiplexer_1_out), .sel(pcsrc));
  Register #(.width(32)) register_1 (.D(multiplexer_1_out), .en(pcload), .Q(register_1_q), .clk(in_24));  // open: clr
  Multiplexer #(.width(32), .enable("false")) multiplexer_2 (
    .in0(register_1_q), .in1(b), .out(multiplexer_2_out), .sel(IOrD));
  Memory memory_1 (
    .Address(multiplexer_2_out), .Input(b), .Clock(in_24), .Load(MemRd), .Store(MemWr), .Data(memory_1_data),
    .Width(width), .Extend(Extend), .DClock(cd));  // open: Clear
  Register #(.width(32)) register_2 (.D(memory_1_data), .en(mdrload), .Q(register_2_q), .clk(cd));  // open: clr
  Register #(.width(32)) register_3 (.D(memory_1_data), .en(IRload), .Q(Inst), .clk(cd));  // open: clr
  Multiplexer #(.width(32), .enable("false")) multiplexer_3 (
    .in0(register_6_q), .in1(register_2_q), .out(multiplexer_3_out), .sel(mem2reg));
  Multiplexer #(.width(5), .enable("false")) multiplexer_4 (
    .in0(rs2), .in1(rd), .out(multiplexer_4_out), .sel(regsrc2));
  regfile regfile_1 (
    .wr(multiplexer_3_out), .r1_a(rs1), .r1_d(regfile_1_r1_d), .r2_a(multiplexer_4_out),
    .r2_d(regfile_1_r2_d), .w_a(rd), .e_en(regwrite), .clk(in_24));
  Register #(.width(32)) register_4 (.D(regfile_1_r1_d), .en(ALoad), .Q(register_4_q), .clk(in_24));  // open: clr
  Register #(.width(32)) register_5 (.D(regfile_1_r2_d), .en(BLoad), .Q(b), .clk(in_24));  // open: clr
  Multiplexer #(.width(32), .enable("false")) multiplexer_5 (
    .in0(register_1_q), .in1(register_4_q), .out(multiplexer_5_out), .sel(alusrc1));
  ALU alu_1 (.Op1(multiplexer_5_out), .op2(multiplexer_6_out), .Sub(sub), .Opcode(opc), .Res(alu_1_res), .C(c), .Z(z));
  Multiplexer #(.select(2), .width(32), .enable("false")) multiplexer_6 (
    .in0(32'h4), .in1(b), .in2(imm), .out(multiplexer_6_out), .sel(alusrc2));  // open: in3
  Register #(.width(32)) register_6 (.D(alu_1_res), .en(aluoutload), .Q(register_6_q), .clk(in_24));  // open: clr

  // Other names for the same wires on the sheet: clk = in_24
endmodule

module control_unit (
  input  [31:0] in_1
);

  wire i, r, s, sb, u, uj;

  Decoder #(.select(5), .tristate("true")) decoder_1 (
    .out0(s), .out2(r), .out3(uj), .out4(i), .out5(u), .out8(s), .out12(r), .out13(u), .out24(sb), .out25(i),
    .out27(uj), .sel(in_1[6:2]));  // open: out1, out6, out7, out9, out10, out11, out14, out15, out16, out17, out18, out19, out20, out21, out22, out23, out26, out28, out29, out30, out31, en
  datapath datapath_1 ();  // open: pcload, in_24, alusrc1, alusrc2, mdrload, mem2reg, regwrite, ALoad, opc, sub, pcsrc, MemWr, IOrD, IRload, Inst, regsrc2, rs1, rs2, rd, BLoad, imm, z, c, MemRd, width, Extend, aluoutload

  // Other names for the same wires on the sheet: inst[31:0] = in_1; opcode[4:0] = in_1[6:2]
endmodule
